// Logisim project sequential-logic.circ as structural Verilog: 5 circuits, main circuit rs-latch
module rs_latch (
  input  r,
  input  s,
  output out,
  output not_out
);

  \nor  nor_1 (.a(r), .b(not_out), .out(out));
  \nor  nor_2 (.a(out), .b(s), .out(not_out));
endmodule

module d_latch (
  input  in,
  input  load,
  output out,
  output not_out
);

  wire and_1_out, and_2_out, not_1_output;

  \not  not_1 (.\input (in), .\output (not_1_output));
  \and  and_1 (.a(not_1_output), .b(load), .out(and_1_out));
  \and  and_2 (.a(in), .b(load), .out(and_2_out));
  rs_latch rs_latch_1 (.r(and_1_out), .s(and_2_out), .out(out), .not_out(not_out));

  // Notes on the sheet:
  //   reset
  //   set
endmodule

module _8_bit_reg (
  input  clk,
  input  wr,
  input  [7:0] in,
  output [7:0] out
);

  wire and_1_out;

  \and  and_1 (.a(clk), .b(wr), .out(and_1_out));
  d_latch d_latch_1 (.in(in[0]), .load(and_1_out), .out(out[0]));  // open: not_out
  d_latch d_latch_2 (.in(in[1]), .load(and_1_out), .out(out[1]));  // open: not_out
  d_latch d_latch_3 (.in(in[2]), .load(and_1_out), .out(out[2]));  // open: not_out
  d_latch d_latch_4 (.in(in[3]), .load(and_1_out), .out(out[3]));  // open: not_out
  d_latch d_latch_5 (.in(in[4]), .load(and_1_out), .out(out[4]));  // open: not_out
  d_latch d_latch_6 (.in(in[5]), .load(and_1_out), .out(out[5]));  // open: not_out
  d_latch d_latch_7 (.in(in[6]), .load(and_1_out), .out(out[6]));  // open: not_out
  d_latch d_latch_8 (.in(in[7]), .load(and_1_out), .out(out[7]));  // open: not_out

  // Notes on the sheet:
  //   clk = global clock
  //   if wr ^ clk:
  //   else:
  //   wr = write input to reg
  //   out(t)=in(t)
  //   out(t)=out(t-1)
  //   clk ^ wr
endmodule

module _4_bit_reg (
  input  clk,
  input  wr,
  input  [3:0] in,
  output [3:0] out
);

  wire and_1_out;

  \and  and_1 (.a(clk), .b(wr), .out(and_1_out));
  d_latch d_latch_1 (.in(in[0]), .load(and_1_out), .out(out[0]));  // open: not_out
  d_latch d_latch_2 (.in(in[1]), .load(and_1_out), .out(out[1]));  // open: not_out
  d_latch d_latch_3 (.in(in[2]), .load(and_1_out), .out(out[2]));  // open: not_out
  d_latch d_latch_4 (.in(in[3]), .load(and_1_out), .out(out[3]));  // open: not_out

  // Notes on the sheet:
  //   if wr ^ clk:
  //   out(t)=in(t)
  //   else:
  //   out(t)=out(t-1)
  //   clk ^ wr
endmodule

module ram4 (
  input  clk,
  input  wr,
  input  [1:0] idx,
  input  [3:0] in
);
endmodule
